// Logisim project 15H_Left_Rotation.circ as structural Verilog: 1 circuit, main circuit main
module main (
  input  [7:0] Input__8_bit,
  input  [2:0] Shift_Amount__3_bit,
  output [7:0] Rotated_Output__8_bit
);

  Shifter #(.width(8), .shift("1r")) shifter_1 (.out(Rotated_Output__8_bit));  // open: in, dist

  // Notes on the sheet:
  //   8-bit Left Rotation Circuit
endmodule
