// Logisim project 17H_Twos_Complement.circ as structural Verilog: 1 circuit, main circuit main
module main (
  input  [7:0] Input__8_bit,
  output [7:0] Twos_Complement__8_bit
);

  wire [7:0] not_1_out;

  // NOT_Gate not_1 has open pins: in=open, out=not_1_out
  // Adder #(.width(8)) adder_1: pin names not known; wires that end beside it: not_1_out, 8'h1, Twos_Complement__8_bit

  // Notes on the sheet:
  //   Two's Complement: Invert + Add 1
endmodule
