// Logisim project 18H_Binary_to_Decimal.circ as structural Verilog: 1 circuit, main circuit main
module main (
  input  [7:0] Input__8_bit
);

  Hex_Digit_Display Hundreds (.value(Input__8_bit[3:0]));  // open: dp
  Hex_Digit_Display Tens (.value(Input__8_bit[3:0]));  // open: dp
  Hex_Digit_Display Ones (.value(Input__8_bit[3:0]));  // open: dp
  // Pins of 4 and 8 bits meet at Input__8_bit

  // Notes on the sheet:
  //   8-bit Binary to Decimal Display
  //   (Uses BCD conversion via splitters)
endmodule
