// Logisim project 1E_NOT_Gate.circ as structural Verilog: 1 circuit, main circuit main
module main (
  input  Input,
  output Output
);

  // NOT_Gate not_1 has open pins: in=open, out=Output
endmodule
