// Logisim project 1H_Clocked_Register.circ as structural Verilog: 1 circuit, main circuit main
module main (
  input  D0,
  input  D1,
  input  D2,
  input  D3,
  input  CLK,
  output Q0,
  output Q1,
  output Q2,
  output Q3
);

  // D_Flip_Flop d_ff_1: pin names not known; wires that end beside it: D0, D0, CLK
  // D_Flip_Flop d_ff_2: pin names not known; wires that end beside it: D1, D1, CLK
  // D_Flip_Flop d_ff_3: pin names not known; wires that end beside it: D2, D2, CLK
  // D_Flip_Flop d_ff_4: pin names not known; wires that end beside it: D3, D3, CLK
endmodule
