// Logisim project 1M_SR_FlipFlop.circ as structural Verilog: 1 circuit, main circuit main
module main (
  input  S__Set,
  input  R__Reset,
  output Q,
  output Q_bar
);

  // NOR_Gate nor_1: pin names not known; wires that end beside it: S__Set, Q_bar, Q
  // NOR_Gate nor_2: pin names not known; wires that end beside it: Q, R__Reset, Q_bar
endmodule
