// Logisim project 22H_Binary_to_Hex.circ as structural Verilog: 1 circuit, main circuit main
module main (
  input  [7:0] Input__8_bit
);

  wire [3:0] undriven, undriven_2;

  Hex_Digit_Display Low_Nibble (.value(undriven));  // open: dp
  Hex_Digit_Display High_Nibble (.value(undriven_2));  // open: dp

  // Notes on the sheet:
  //   8-bit Binary to Hexadecimal
endmodule
