// Logisim project 2H_Bit_Reversal_Register.circ as structural Verilog: 1 circuit, main circuit main
module main (
  input  In7__MSB,
  input  In6,
  input  In5,
  input  In4,
  input  In3,
  input  In2,
  input  In1,
  input  In0__LSB,
  output Out7___In0,
  output Out6___In1,
  output Out5___In2,
  output Out4___In3,
  output Out3___In4,
  output Out2___In5,
  output Out1___In6,
  output Out0___In7
);


  assign Out0___In7 = In7__MSB;
  assign Out1___In6 = In6;
  assign Out2___In5 = In5;
  assign Out3___In4 = In4;
  assign Out4___In3 = In3;
  assign Out5___In2 = In2;
  assign Out6___In1 = In1;
  assign Out7___In0 = In0__LSB;
endmodule
