// Logisim project 3H_Delay_Circuit.circ as structural Verilog: 1 circuit, main circuit main
module main (
  input  Input,
  input  CLK,
  output Delayed_Output__4_cycles
);

  wire d_ff_2_q, d_ff_3_q, d_ff_4_q;

  // D_Flip_Flop d_ff_1: pin names not known; wires that end beside it: Input, Input, CLK
  D_Flip_Flop d_ff_2 (.clk(d_ff_2_q), .Q(d_ff_2_q), .Qn(CLK));  // open: D, preset, en, reset
  D_Flip_Flop d_ff_3 (.clk(d_ff_3_q), .Q(d_ff_3_q), .Qn(CLK));  // open: D, preset, en, reset
  D_Flip_Flop d_ff_4 (.clk(d_ff_4_q), .Q(d_ff_4_q), .Qn(CLK));  // open: D, preset, en, reset

  // Notes on the sheet:
  //   4-Clock-Cycle Delay Circuit
endmodule
