// Logisim project 5H_4bit_Comparator.circ as structural Verilog: 1 circuit, main circuit main
module main (
  input  A3,
  input  A2,
  input  A1,
  input  A0,
  input  B3,
  input  B2,
  input  B1,
  input  B0,
  output A_greater_than_B,
  output A_equals_B,
  output A_less_than_B
);

  // Comparator #(.width(4)) comparator_1: pin names not known; wires that end beside it: A3, A2, A1, A0, A_greater_than_B, A_equals_B
endmodule
