// Logisim project 6H_4to16_Decoder.circ as structural Verilog: 1 circuit, main circuit main
module main (
  input  A3__MSB,
  input  A2,
  input  A1,
  input  A0__LSB,
  output Y0,
  output Y1,
  output Y2,
  output Y3,
  output Y4,
  output Y5,
  output Y6,
  output Y7,
  output Y8,
  output Y9,
  output Y10,
  output Y11,
  output Y12,
  output Y13,
  output Y14,
  output Y15
);

  // Decoder #(.select(4)) decoder_1: pin names not known; wires that end beside it: Y0, Y1, Y2, Y3
endmodule
