// Logisim project 7H_Priority_Encoder.circ as structural Verilog: 1 circuit, main circuit main
module main (
  input  I3__Highest_Priority,
  input  I2,
  input  I1,
  input  I0__Lowest_Priority,
  output Out1__MSB,
  output Out0__LSB,
  output Group_Signal
);

  // Priority_Encoder #(.select(2)) priority_encoder_1: pin names not known; wires that end beside it: I3__Highest_Priority, I2, I1, I0__Lowest_Priority, Out1__MSB, Out0__LSB, Group_Signal
endmodule
