// Logisim project 7M_Binary_to_Decimal.circ as structural Verilog: 1 circuit, main circuit main
module main (
  input  Bit3__MSB,
  input  Bit2,
  input  Bit1,
  input  Bit0__LSB
);

  wire [3:0] undriven;

  Hex_Digit_Display hex_digit_display_1 (.value(undriven));  // open: dp
endmodule
