// Logisim project 8H_8bit_Full_Adder.circ as structural Verilog: 1 circuit, main circuit main
module main (
  input  [7:0] A__8_bit,
  input  [7:0] B__8_bit,
  input  Carry_In,
  output [7:0] Sum__8_bit,
  output Carry_Out
);

  // Adder #(.width(8)) adder_1: pin names not known; wires that end beside it: A__8_bit, B__8_bit, Carry_In, Sum__8_bit, Carry_Out
endmodule
