// Logisim project 9M_2Input_Multiplexer.circ as structural Verilog: 1 circuit, main circuit main
module main (
  input  I0,
  input  I1,
  input  Sel,
  output Output
);

  wire and_1_p3, and_2_p3, not_1_out;

  not not_1 (not_1_out, Sel);
  // AND_Gate and_1: pin names not known; wires that end beside it: I0, not_1_out, and_1_p3
  // AND_Gate and_2: pin names not known; wires that end beside it: I1, Sel, and_2_p3
  // OR_Gate or_1: pin names not known; wires that end beside it: and_1_p3, and_2_p3, Output
endmodule
