// Logisim project 15H_Left_Rotation.circ as structural Verilog: 1 circuit, main circuit main
module main (
  input  [7:0] Data__8_bit,
  input  [2:0] Amount__3_bit,
  output [7:0] Rotated__8_bit
);

  Shifter #(.width(8), .shift("1r")) shifter_1 (.in(Data__8_bit), .\dist (Amount__3_bit), .out(Rotated__8_bit));

  // Notes on the sheet:
  //   Exercise 15H: 8-bit Left Rotation
  //   Bits shifted left wrap around to the right side
  //   e.g. 10000001 rotated left by 2 = 00000110
endmodule
