// Logisim project 17H_Twos_Complement.circ as structural Verilog: 1 circuit, main circuit main
module main (
  input  [7:0] Input__8_bit,
  output [7:0] Result__8_bit,
  output Overflow
);

  wire [7:0] not_1_out;

  // NOT_Gate not_1 has open pins: in=open, out=not_1_out
  Adder #(.width(8)) adder_1 (.a(not_1_out), .b(8'h1));  // open: out, cin, cout

  // Notes on the sheet:
  //   Exercise 17H: 8-bit Two's Complement
  //   Result = NOT(Input) + 1 = -Input
  //   Step 1: Invert all bits (one's complement)
  //   Step 2: Add 1 to get two's complement
endmodule
