// Logisim project 18H_Binary_to_Decimal.circ as structural Verilog: 1 circuit, main circuit main
module main (
  input  [7:0] Input__8_bit
);

  wire [3:0] undriven;

  Hex_Digit_Display hex_digit_display_1 (.value(undriven));  // open: dp
  Hex_Digit_Display hex_digit_display_2 (.value(Input__8_bit[7:4]));  // open: dp

  // Notes on the sheet:
  //   High
  //   Displays 8-bit value as two hex digits
  //   For decimal: value = High*16 + Low
  //   e.g. Input=11111111 shows FF (=255 decimal)
  //   Exercise 18H: 8-bit Binary to Decimal Display
  //   Low
endmodule
