// Logisim project 1E_NOT_Gate.circ as structural Verilog: 1 circuit, main circuit main
module main (
  input  A,
  output NOT_A
);

  // NOT_Gate not_1 has open pins: in=open, out=NOT_A

  // Notes on the sheet:
  //   Exercise 1E: NOT Gate (Inverter)
  //   Output = NOT(A)
endmodule
