// Logisim project 1H_Clocked_Register.circ as structural Verilog: 1 circuit, main circuit main
module main (
  input  D0,
  input  D1,
  input  D2,
  input  D3,
  input  CLK,
  output Q0,
  output Q1,
  output Q2,
  output Q3
);

  wire d_ff_2_p2, d_ff_3_p2, d_ff_4_p2;

  // D_Flip_Flop d_ff_1: pin names not known; wires that end beside it: D0, CLK, Q0
  // D_Flip_Flop d_ff_2: pin names not known; wires that end beside it: D1, d_ff_2_p2, Q1
  // D_Flip_Flop d_ff_3: pin names not known; wires that end beside it: D2, d_ff_3_p2, Q2
  // D_Flip_Flop d_ff_4: pin names not known; wires that end beside it: D3, d_ff_4_p2, Q3

  // Notes on the sheet:
  //   Exercise 1H: 4-bit Clocked Register
  //   All flip-flops share the same clock
  //   Data captured on rising edge of CLK
endmodule
