// Logisim project 1M_SR_FlipFlop.circ as structural Verilog: 1 circuit, main circuit main
module main (
  input  S__Set,
  input  R__Reset,
  output Q,
  output Q_bar
);

  wire nor_1_p2, nor_2_p1;

  // NOR_Gate nor_1: pin names not known; wires that end beside it: S__Set, nor_1_p2, Q
  // NOR_Gate nor_2: pin names not known; wires that end beside it: nor_2_p1, R__Reset, Q_bar

  // Notes on the sheet:
  //   Exercise 1M: SR Flip-Flop (NOR gates)
endmodule
