// Logisim project 22H_Binary_to_Hex.circ as structural Verilog: 1 circuit, main circuit main
module main (
  input  [7:0] Input__8_bit
);

  wire [3:0] undriven;

  Hex_Digit_Display hex_digit_display_1 (.value(undriven));  // open: dp
  Hex_Digit_Display hex_digit_display_2 (.value(Input__8_bit[7:4]));  // open: dp

  // Notes on the sheet:
  //   High Nibble
  //   Exercise 22H: 8-bit Binary to Hexadecimal
  //   Low Nibble
  //   8 bits split into two 4-bit groups
  //   Each group = one hex digit (0-F)
  //   e.g. 10101111 = AF in hex
endmodule
