// Logisim project 3H_Delay_Circuit.circ as structural Verilog: 1 circuit, main circuit main
module main (
  input  Input,
  input  CLK,
  output Delayed_Out
);

  wire d_ff_1_p2, d_ff_1_p3, d_ff_2_p2, d_ff_2_p3, d_ff_3_p2, d_ff_3_p3, d_ff_4_p2;

  // D_Flip_Flop d_ff_1: pin names not known; wires that end beside it: Input, d_ff_1_p2, d_ff_1_p3
  // D_Flip_Flop d_ff_2: pin names not known; wires that end beside it: d_ff_1_p3, d_ff_2_p2, d_ff_2_p3
  // D_Flip_Flop d_ff_3: pin names not known; wires that end beside it: d_ff_2_p3, d_ff_3_p2, d_ff_3_p3
  // D_Flip_Flop d_ff_4: pin names not known; wires that end beside it: d_ff_3_p3, d_ff_4_p2, Delayed_Out

  // Notes on the sheet:
  //   Exercise 3H: 4-Clock-Cycle Delay Line
  //   Signal appears at output after 4 rising clock edges
endmodule
