// Logisim project 5H_4bit_Comparator.circ as structural Verilog: 1 circuit, main circuit main
module main (
  input  [3:0] A__4_bit,
  input  [3:0] B__4_bit,
  output A_greater_B,
  output A_equals_B,
  output A_less_B
);

  Comparator #(.width(4)) comparator_1 (.a(A__4_bit), .b(B__4_bit), .gt(A_greater_B), .eq(A_equals_B), .lt(A_less_B));

  // Notes on the sheet:
  //   Exercise 5H: 4-bit Comparator
  //   Compares two 4-bit unsigned numbers
  //   Exactly one output is HIGH at any time
endmodule
