// Logisim project 7H_Priority_Encoder.circ as structural Verilog: 1 circuit, main circuit main
module main (
  input  I0__Lowest,
  input  I1,
  input  I2,
  input  I3__Highest,
  output Out1__MSB,
  output Out0__LSB,
  output Group_Signal
);

  // Priority_Encoder #(.select(2)) priority_encoder_1: pin names not known; wires that end beside it: I0__Lowest, I1, I2, I3__Highest, Out1__MSB, Out0__LSB, Group_Signal

  // Notes on the sheet:
  //   Exercise 7H: 4-input Priority Encoder
  //   Encodes the highest-priority active input
  //   If I3 and I1 both HIGH, output = 11 (binary 3)
endmodule
