// Logisim project 7M_Binary_to_Decimal.circ as structural Verilog: 1 circuit, main circuit main
module main (
  input  [3:0] Binary__4_bit
);

  Hex_Digit_Display hex_digit_display_1 (.value(Binary__4_bit));  // open: dp

  // Notes on the sheet:
  //   Exercise 7M: 4-bit Binary to Decimal
  //   Displays decimal value 0-15
  //   Set pin value to test (e.g. 0101 = 5)
endmodule
