// Logisim project 8H_8bit_Full_Adder.circ as structural Verilog: 1 circuit, main circuit main
module main (
  input  [7:0] A__8_bit,
  input  [7:0] B__8_bit,
  input  Carry_In,
  output [7:0] Sum__8_bit,
  output Carry_Out
);

  Adder #(.width(8)) adder_1 (.a(A__8_bit), .b(B__8_bit), .cout(Carry_In));  // open: out, cin

  // Notes on the sheet:
  //   Exercise 8H: 8-bit Full Adder
  //   Adds two 8-bit numbers with carry propagation
  //   Carry Out = 1 when result exceeds 255
endmodule
