// Logisim project 9M_2Input_Multiplexer.circ as structural Verilog: 1 circuit, main circuit main
module main (
  input  I0,
  input  I1,
  input  Sel,
  output Y
);

  wire and_1_out, and_2_out, not_1_out, undriven;

  not not_1 (not_1_out, Sel);
  and and_1 (and_1_out, I0, not_1_out);
  and and_2 (and_2_out, I1, undriven);
  or or_1 (Y, and_1_out, and_2_out);

  // Notes on the sheet:
  //   Exercise 9M: 2-to-1 Multiplexer
  //   Y = I0*NOT(Sel) + I1*Sel
endmodule
