// Logisim project 16H_Bitwise_Negation.circ as structural Verilog: 1 circuit, main circuit main
module main (
  input  In7,
  input  In6,
  input  In5,
  input  In4,
  input  In3,
  input  In2,
  input  In1,
  input  In0,
  output Out7,
  output Out6,
  output Out5,
  output Out4,
  output Out3,
  output Out2,
  output Out1,
  output Out0
);

  // NOT_Gate not_1 has open pins: in=In7, out=open
  // NOT_Gate not_2 has open pins: in=In6, out=open
  // NOT_Gate not_3 has open pins: in=In5, out=open
  // NOT_Gate not_4 has open pins: in=In4, out=open
  // NOT_Gate not_5 has open pins: in=In3, out=open
  // NOT_Gate not_6 has open pins: in=In2, out=open
  // NOT_Gate not_7 has open pins: in=In1, out=open
  // NOT_Gate not_8 has open pins: in=In0, out=open

  // Notes on the sheet:
  //   Exercise 16H: 8-bit Bitwise Negation
  //   Out[i] = NOT(In[i])
endmodule
