// Logisim project 16H_Bitwise_Negation_v2.circ as structural Verilog: 1 circuit, main circuit main
module main (
  input  In7,
  input  In6,
  input  In5,
  input  In4,
  input  In3,
  input  In2,
  input  In1,
  input  In0,
  output Out7,
  output Out6,
  output Out5,
  output Out4,
  output Out3,
  output Out2,
  output Out1,
  output Out0
);

  not not_1 (Out7, In7);
  not not_2 (Out6, In6);
  not not_3 (Out5, In5);
  not not_4 (Out4, In4);
  not not_5 (Out3, In3);
  not not_6 (Out2, In2);
  not not_7 (Out1, In1);
  not not_8 (Out0, In0);

  // Notes on the sheet:
  //   Exercise 16H: 8-bit Bitwise Negation
  //   Out[i] = NOT(In[i])
endmodule
