// Logisim project 2H_Bit_Reversal_Register_v5.circ as structural Verilog: 1 circuit, main circuit main
module main (
  input  In6,
  input  In4,
  input  In2,
  input  In0,
  output Out0,
  output Out1,
  output Out2,
  output Out3,
  output Out4,
  output Out5,
  output Out6,
  output Out7
);


  assign Out0 = In0;
  assign Out1 = 1'b1;
  assign Out2 = In2;
  assign Out3 = 1'b1;
  assign Out4 = In4;
  assign Out5 = 1'b1;
  assign Out6 = In6;
  assign Out7 = 1'b1;

  // Other names for the same wires on the sheet: B0 = In0; B2 = In2; B4 = In4; B6 = In6

  // Notes on the sheet:
  //   In7
  //   In5
  //   In3
  //   In1
  //   Exercise 2H: 8-bit Bit Reversal
  //   In[i] maps to Out[7-i]
endmodule
