// Logisim project 6H_4to16_Decoder_v2.circ as structural Verilog: 1 circuit, main circuit main
module main (
  input  [3:0] A_3_0,
  output Y0,
  output Y1,
  output Y2,
  output Y3,
  output Y4,
  output Y5,
  output Y6,
  output Y7,
  output Y8,
  output Y9,
  output Y10,
  output Y11,
  output Y12,
  output Y13,
  output Y14,
  output Y15
);

  // Decoder #(.select(4), .disabled("ZERO")) decoder_1: pin names not known; wires that end beside it: A_3_0, Y0, Y1, Y2, Y3, Y4, Y5, Y6, Y7, Y8, Y9, Y10, Y11, Y12, Y13, Y14, Y15

  // Notes on the sheet:
  //   Exercise 6H: 4-to-16 Decoder
  //   One-hot output: exactly one Y is high for each input value
endmodule
