// Logisim project 6H_4to16_Decoder_v3.circ as structural Verilog: 1 circuit, main circuit main
module main (
  input  A3,
  input  A2,
  input  A1,
  input  A0,
  output Y0,
  output Y1,
  output Y2,
  output Y3,
  output Y4,
  output Y5,
  output Y6,
  output Y7,
  output Y8,
  output Y9,
  output Y10,
  output Y11,
  output Y12,
  output Y13,
  output Y14,
  output Y15
);

  wire nA0, nA1, nA2, nA3, undriven, undriven_2, undriven_3, undriven_4, undriven_5, undriven_6, undriven_7,
       undriven_8, undriven_9, undriven_10, undriven_11, undriven_12, undriven_13, undriven_14, undriven_15;

  not not_1 (nA3, A3);
  not not_2 (nA2, A2);
  not not_3 (nA1, A1);
  not not_4 (nA0, A0);
  buf and_1 (Y0, undriven);  // AND_Gate
  and and_2 (Y1, undriven, undriven_2);
  and and_3 (Y2, undriven_2, undriven_3);
  and and_4 (Y3, undriven_3, undriven_4);
  and and_5 (Y4, undriven_4, undriven_5);
  and and_6 (Y5, undriven_5, undriven_6);
  and and_7 (Y6, undriven_6, undriven_7);
  and and_8 (Y7, undriven_7, undriven_8);
  and and_9 (Y8, undriven_8, undriven_9);
  and and_10 (Y9, undriven_9, undriven_10);
  and and_11 (Y10, undriven_10, undriven_11);
  and and_12 (Y11, undriven_11, undriven_12);
  and and_13 (Y12, undriven_12, undriven_13);
  and and_14 (Y13, undriven_13, undriven_14);
  and and_15 (Y14, undriven_14, undriven_15);
  buf and_16 (Y15, undriven_15);  // AND_Gate

  // Notes on the sheet:
  //   Exercise 6H: 4-to-16 Decoder
  //   One-hot: exactly one Y is high per input
endmodule
