// Logisim project 6H_4to16_Decoder_v6.circ as structural Verilog: 1 circuit, main circuit main
module main (
  input  A3,
  input  A2,
  input  A1,
  input  A0,
  output Y0,
  output Y1,
  output Y2,
  output Y3,
  output Y4,
  output Y5,
  output Y6,
  output Y7,
  output Y8,
  output Y9,
  output Y10,
  output Y11,
  output Y12,
  output Y13,
  output Y14,
  output Y15
);

  wire and_1_p1, and_1_p2, and_1_p3, and_1_p4, and_1_p5, and_2_p3, and_2_p4, and_2_p5, and_2_p6, and_3_p3,
       and_3_p4, and_3_p5, and_3_p6, and_4_p3, and_4_p4, and_4_p5, and_4_p6, and_5_p3, and_5_p4, and_5_p5,
       and_5_p6, and_6_p3, and_6_p4, and_6_p5, and_6_p6, and_7_p3, and_7_p4, and_7_p5, and_8_p3, and_8_p4,
       and_8_p5, and_8_p6, and_9_p3, and_9_p4, and_9_p5, and_9_p6, and_10_p3, and_10_p4, and_10_p5,
       and_10_p6, and_11_p3, and_11_p4, and_11_p5, and_11_p6, and_12_p4, and_12_p5, and_12_p6, and_13_p3,
       and_13_p4, and_13_p5, and_13_p6, and_14_p3, and_14_p5, and_14_p6, and_15_p3, and_15_p4, not_1_out,
       not_2_out, not_3_out, not_4_out;

  not not_1 (not_1_out, A3);
  not not_2 (not_2_out, A2);
  not not_3 (not_3_out, A1);
  not not_4 (not_4_out, A0);
  // AND_Gate and_1: pin names not known; wires that end beside it: and_1_p1, and_1_p2, and_1_p3, and_1_p4, and_1_p5, Y0
  // AND_Gate and_2: pin names not known; wires that end beside it: and_1_p4, and_1_p5, and_2_p3, and_2_p4, and_2_p5, and_2_p6, Y1
  // AND_Gate and_3: pin names not known; wires that end beside it: and_2_p5, and_2_p6, and_3_p3, and_3_p4, and_3_p5, and_3_p6, Y2
  // AND_Gate and_4: pin names not known; wires that end beside it: and_3_p5, and_3_p6, and_4_p3, and_4_p4, and_4_p5, and_4_p6, Y3
  // AND_Gate and_5: pin names not known; wires that end beside it: and_4_p5, and_4_p6, and_5_p3, and_5_p4, and_5_p5, and_5_p6, Y4
  // AND_Gate and_6: pin names not known; wires that end beside it: and_5_p5, and_5_p6, and_6_p3, and_6_p4, and_6_p5, and_6_p6, Y5
  // AND_Gate and_7: pin names not known; wires that end beside it: and_6_p5, and_6_p6, and_7_p3, and_7_p4, and_7_p5, not_1_out, Y6
  // AND_Gate and_8: pin names not known; wires that end beside it: and_7_p5, not_1_out, and_8_p3, and_8_p4, and_8_p5, and_8_p6, Y7
  // AND_Gate and_9: pin names not known; wires that end beside it: and_8_p5, and_8_p6, and_9_p3, and_9_p4, and_9_p5, and_9_p6, Y8
  // AND_Gate and_10: pin names not known; wires that end beside it: and_9_p5, and_9_p6, and_10_p3, and_10_p4, and_10_p5, and_10_p6, Y9
  // AND_Gate and_11: pin names not known; wires that end beside it: and_10_p5, and_10_p6, and_11_p3, and_11_p4, and_11_p5, and_11_p6, Y10
  // AND_Gate and_12: pin names not known; wires that end beside it: and_11_p5, and_11_p6, not_2_out, and_12_p4, and_12_p5, and_12_p6, Y11
  // AND_Gate and_13: pin names not known; wires that end beside it: and_12_p5, and_12_p6, and_13_p3, and_13_p4, and_13_p5, and_13_p6, Y12
  // AND_Gate and_14: pin names not known; wires that end beside it: and_13_p5, and_13_p6, and_14_p3, not_3_out, and_14_p5, and_14_p6, Y13
  // AND_Gate and_15: pin names not known; wires that end beside it: and_14_p5, and_14_p6, and_15_p3, and_15_p4, not_4_out, A3, Y14
  // AND_Gate and_16: pin names not known; wires that end beside it: not_4_out, A3, A2, A1, A0, Y15

  // Notes on the sheet:
  //   Exercise 6H: 4-to-16 Decoder
  //   One-hot: exactly one Y is high per input
endmodule
