// Logisim project 6H_4to16_Decoder_v7.circ as structural Verilog: 1 circuit, main circuit main
module main (
  input  A3,
  input  A2,
  input  A1,
  input  A0,
  output Y0,
  output Y1,
  output Y2,
  output Y3,
  output Y4,
  output Y5,
  output Y6,
  output Y7,
  output Y8,
  output Y9,
  output Y10,
  output Y11,
  output Y12,
  output Y13,
  output Y14,
  output Y15
);

  wire N0, N1, N2, N3, T0, T1, T2, T3;

  not not_1 (N3, A3);
  not not_2 (N2, A2);
  not not_3 (N1, A1);
  not not_4 (N0, A0);
  // AND_Gate and_1: pin names not known; wires that end beside it: N3, N2, N1, N0, N3, Y0
  // AND_Gate and_2: pin names not known; wires that end beside it: N0, N3, N2, N1, T0, N3, Y1
  // AND_Gate and_3: pin names not known; wires that end beside it: T0, N3, N2, T1, N0, N3, Y2
  // AND_Gate and_4: pin names not known; wires that end beside it: N0, N3, N2, T1, T0, N3, Y3
  // AND_Gate and_5: pin names not known; wires that end beside it: T0, N3, T2, N1, N0, N3, Y4
  // AND_Gate and_6: pin names not known; wires that end beside it: N0, N3, T2, N1, T0, N3, Y5
  // AND_Gate and_7: pin names not known; wires that end beside it: T0, N3, T2, T1, N0, N3, Y6
  // AND_Gate and_8: pin names not known; wires that end beside it: N0, N3, T2, T1, T0, T3, Y7
  // AND_Gate and_9: pin names not known; wires that end beside it: T0, T3, N2, N1, N0, T3, Y8
  // AND_Gate and_10: pin names not known; wires that end beside it: N0, T3, N2, N1, T0, T3, Y9
  // AND_Gate and_11: pin names not known; wires that end beside it: T0, T3, N2, T1, N0, T3, Y10
  // AND_Gate and_12: pin names not known; wires that end beside it: N0, T3, N2, T1, T0, T3, Y11
  // AND_Gate and_13: pin names not known; wires that end beside it: T0, T3, T2, N1, N0, T3, Y12
  // AND_Gate and_14: pin names not known; wires that end beside it: N0, T3, T2, N1, T0, T3, Y13
  // AND_Gate and_15: pin names not known; wires that end beside it: T0, T3, T2, T1, N0, T3, Y14
  // AND_Gate and_16: pin names not known; wires that end beside it: N0, T3, T2, T1, T0, Y15

  // Notes on the sheet:
  //   Exercise 6H: 4-to-16 Decoder
  //   One-hot: exactly one Y is high per input
endmodule
