// Logisim project 6H_4to16_Decoder_v8.circ as structural Verilog: 1 circuit, main circuit main
module main (
  input  A3,
  input  A2,
  input  A1,
  input  A0,
  output Y0,
  output Y1,
  output Y2,
  output Y3,
  output Y4,
  output Y5,
  output Y6,
  output Y7,
  output Y8,
  output Y9,
  output Y10,
  output Y11,
  output Y12,
  output Y13,
  output Y14,
  output Y15
);

  wire [3:0] decoder_1_p1;

  // Decoder #(.select(4), .disabled("ZERO")) decoder_1: pin names not known; wires that end beside it: decoder_1_p1, Y0, Y1, Y2, Y3, Y4, Y5, Y6, Y7, Y8, Y9, Y10

  assign A1 = A0;
  assign A3 = A2;

  // Notes on the sheet:
  //   Exercise 6H: 4-to-16 Decoder
  //   One-hot: exactly one Y is high per input
endmodule
