// Logisim project 6H_4to16_Decoder_v9.circ as structural Verilog: 1 circuit, main circuit main
module main (
  input  A3,
  input  A2,
  input  A1,
  input  A0,
  output Y0,
  output Y1,
  output Y2,
  output Y3,
  output Y4,
  output Y5,
  output Y6,
  output Y7,
  output Y8,
  output Y9,
  output Y10,
  output Y11,
  output Y12,
  output Y13,
  output Y14,
  output Y15
);

  wire and_1_p1, and_1_p2, and_1_p4, and_1_p5, and_1_p6, and_1_p7, and_2_p6, and_2_p7, and_2_p8, and_2_p9,
       and_3_p6, and_3_p7, and_3_p8, and_3_p9, and_4_p6, and_4_p7, and_4_p8, and_4_p9, and_5_p6, and_5_p7,
       and_5_p8, and_5_p9, and_6_p6, and_6_p7, and_6_p8, and_6_p9, and_7_p6, and_7_p7, and_7_p8, and_7_p9,
       and_8_p6, and_8_p7, and_8_p8, and_8_p9, and_9_p6, and_9_p7, and_9_p8, and_9_p9, and_10_p6, and_10_p7,
       and_10_p8, and_10_p9, and_11_p6, and_11_p7, and_11_p8, and_11_p9, and_12_p6, and_12_p7, and_12_p8,
       and_12_p9, and_13_p6, and_13_p7, and_13_p8, and_13_p9, and_14_p6, and_14_p7, and_14_p8, and_14_p9,
       and_15_p6, and_15_p7, and_15_p8, and_15_p9, and_16_p6, and_16_p7, not_1_out, not_2_out, not_3_out,
       not_4_out;

  not not_1 (not_1_out, A3);
  not not_2 (not_2_out, A2);
  not not_3 (not_3_out, A1);
  not not_4 (not_4_out, A0);
  // AND_Gate and_1: pin names not known; wires that end beside it: and_1_p1, and_1_p2, Y0, and_1_p4, and_1_p5, and_1_p6, and_1_p7
  // AND_Gate and_2: pin names not known; wires that end beside it: and_1_p4, and_1_p5, and_1_p6, and_1_p7, Y1, and_2_p6, and_2_p7, and_2_p8, and_2_p9
  // AND_Gate and_3: pin names not known; wires that end beside it: and_2_p6, and_2_p7, and_2_p8, and_2_p9, Y2, and_3_p6, and_3_p7, and_3_p8, and_3_p9
  // AND_Gate and_4: pin names not known; wires that end beside it: and_3_p6, and_3_p7, and_3_p8, and_3_p9, Y3, and_4_p6, and_4_p7, and_4_p8, and_4_p9
  // AND_Gate and_5: pin names not known; wires that end beside it: and_4_p6, and_4_p7, and_4_p8, and_4_p9, Y4, and_5_p6, and_5_p7, and_5_p8, and_5_p9
  // AND_Gate and_6: pin names not known; wires that end beside it: and_5_p6, and_5_p7, and_5_p8, and_5_p9, Y5, and_6_p6, and_6_p7, and_6_p8, and_6_p9
  // AND_Gate and_7: pin names not known; wires that end beside it: and_6_p6, and_6_p7, and_6_p8, and_6_p9, Y6, and_7_p6, and_7_p7, and_7_p8, and_7_p9
  // AND_Gate and_8: pin names not known; wires that end beside it: and_7_p6, and_7_p7, and_7_p8, and_7_p9, Y7, and_8_p6, and_8_p7, and_8_p8, and_8_p9
  // AND_Gate and_9: pin names not known; wires that end beside it: and_8_p6, and_8_p7, and_8_p8, and_8_p9, Y8, and_9_p6, and_9_p7, and_9_p8, and_9_p9
  // AND_Gate and_10: pin names not known; wires that end beside it: and_9_p6, and_9_p7, and_9_p8, and_9_p9, Y9, and_10_p6, and_10_p7, and_10_p8, and_10_p9
  // AND_Gate and_11: pin names not known; wires that end beside it: and_10_p6, and_10_p7, and_10_p8, and_10_p9, Y10, and_11_p6, and_11_p7, and_11_p8, and_11_p9
  // AND_Gate and_12: pin names not known; wires that end beside it: and_11_p6, and_11_p7, and_11_p8, and_11_p9, Y11, and_12_p6, and_12_p7, and_12_p8, and_12_p9
  // AND_Gate and_13: pin names not known; wires that end beside it: and_12_p6, and_12_p7, and_12_p8, and_12_p9, Y12, and_13_p6, and_13_p7, and_13_p8, and_13_p9
  // AND_Gate and_14: pin names not known; wires that end beside it: and_13_p6, and_13_p7, and_13_p8, and_13_p9, Y13, and_14_p6, and_14_p7, and_14_p8, and_14_p9
  // AND_Gate and_15: pin names not known; wires that end beside it: and_14_p6, and_14_p7, and_14_p8, and_14_p9, Y14, and_15_p6, and_15_p7, and_15_p8, and_15_p9
  // AND_Gate and_16: pin names not known; wires that end beside it: and_15_p6, and_15_p7, and_15_p8, and_15_p9, Y15, and_16_p6, and_16_p7

  // Notes on the sheet:
  //   Exercise 6H: 4-to-16 Decoder
  //   One-hot: exactly one Y is high per input
endmodule
