// Logisim project TEST_DECODER_V2.circ as structural Verilog: 1 circuit, main circuit main
module main (
  input  [3:0] sel_west,
  input  [3:0] sel_south,
  output Y0,
  output Y15
);

  // Decoder #(.select(4)) decoder_1: pin names not known; wires that end beside it: sel_west, Y0

  // Notes on the sheet:
  //   Try select on south: wire to (280,280)
  //   Also try: wire from (260,100) going left
  //   DECODER PIN TEST - select=4, 16 outputs
endmodule
