// Logisim project TEST_HEX_V2.circ as structural Verilog: 1 circuit, main circuit main
module main (
  input  [3:0] B_in,
  input  [3:0] A_in,
  input  [3:0] C_in,
  input  [3:0] D_in,
  input  [3:0] E_in,
  input  [3:0] F_in
);

  Hex_Digit_Display hex_digit_display_1 (.value(A_in));  // open: dp
  // Hex_Digit_Display hex_digit_display_2: pin names not known; wires that end beside it: C_in
  // Hex_Digit_Display hex_digit_display_3: pin names not known; wires that end beside it: E_in
  Hex_Digit_Display hex_digit_display_4 (.value(B_in));  // open: dp
  // Hex_Digit_Display hex_digit_display_5: pin names not known; wires that end beside it: D_in
  Hex_Digit_Display hex_digit_display_6 (.value(F_in));  // open: dp

  // Notes on the sheet:
  //   Method A: wire to loc from LEFT
  //   Method C: wire THROUGH loc vertically
  //   Method E: Splitter(facing south) output below to display
  //   HEX DISPLAY PIN TEST - which method connects?
  //   Method B: wire to loc from ABOVE
  //   Method D: wire ends at loc+0,+30 (below display)
  //   Method F: loc=(500,500), wire from (500,460) to (500,500)
endmodule
