// Logisim project 15H_Left_Rotation.circ as structural Verilog: 1 circuit, main circuit main
module main (
  input  [7:0] Data,
  input  [2:0] Amount,
  output [7:0] Rotated
);

  Shifter #(.width(8), .shift("1r")) shifter_1 (.in(Data), .\dist (Amount), .out(Rotated));

  // Notes on the sheet:
  //   Exercise 15H: 8-bit Left Rotation
endmodule
