// Logisim project 16H_Bitwise_Negation.circ as structural Verilog: 1 circuit, main circuit main
module main (
  input  Bit7,
  input  Bit6,
  input  Bit5,
  input  Bit4,
  input  Bit3,
  input  Bit2,
  input  Bit1,
  input  Bit0,
  output NotBit7,
  output NotBit6,
  output NotBit5,
  output NotBit4,
  output NotBit3,
  output NotBit2,
  output NotBit1,
  output NotBit0
);

  not not_1 (NotBit7, Bit7);
  not not_2 (NotBit6, Bit6);
  not not_3 (NotBit5, Bit5);
  not not_4 (NotBit4, Bit4);
  not not_5 (NotBit3, Bit3);
  not not_6 (NotBit2, Bit2);
  not not_7 (NotBit1, Bit1);
  not not_8 (NotBit0, Bit0);

  // Notes on the sheet:
  //   Exercise 16H: 8-bit Bitwise Negation
  //   Each bit passes through its own NOT gate
endmodule
