// Logisim project 17H_Twos_Complement.circ as structural Verilog: 1 circuit, main circuit main
module main (
  input  [7:0] Input,
  output [7:0] Result,
  output Overflow
);

  wire [7:0] not_1_out;

  assign not_1_out = ~Input;  // NOT_Gate not_1, 8 bits wide
  Adder #(.width(8)) adder_1 (.a(not_1_out), .b(8'h1));  // open: out, cin, cout

  // Notes on the sheet:
  //   Exercise 17H: 8-bit Twos Complement
  //   Result = NOT(Input) + 1
endmodule
