// Logisim project 18H_Binary_to_Decimal.circ as structural Verilog: 1 circuit, main circuit main
module main (
  input  [7:0] Input_8bit
);

  // Hex_Digit_Display hex_digit_display_1: pin names not known
  // Hex_Digit_Display hex_digit_display_2: pin names not known

  // Notes on the sheet:
  //   High Nibble
  //   Exercise 18H: 8-bit Binary to Decimal Display
  //   Splits 8-bit input into two 4-bit nibbles for display
  //   Low Nibble
endmodule
