// Logisim project 1E_NOT_Gate.circ as structural Verilog: 1 circuit, main circuit main
module main (
  input  A,
  output NOT_A
);

  not not_1 (NOT_A, A);

  // Notes on the sheet:
  //   Exercise 1E: NOT Gate
  //   Input A passes through a NOT gate to produce NOT_A
endmodule
