// Logisim project 1M_SR_FlipFlop.circ as structural Verilog: 1 circuit, main circuit main
module main (
  input  S,
  input  R,
  output Q,
  output Qbar
);

  // NOR_Gate nor_1: pin names not known; wires that end beside it: S, Qbar, Q
  // NOR_Gate nor_2: pin names not known; wires that end beside it: Q, R, Qbar

  // Notes on the sheet:
  //   Exercise 1M: SR Flip-Flop (cross-coupled NOR gates)
endmodule
