// Logisim project 22H_Binary_to_Hex.circ as structural Verilog: 1 circuit, main circuit main
module main (
  input  [7:0] Input_8bit
);

  // Hex_Digit_Display hex_digit_display_1: pin names not known
  // Hex_Digit_Display hex_digit_display_2: pin names not known

  // Notes on the sheet:
  //   High Nibble
  //   Exercise 22H: 8-bit Binary to Hexadecimal
  //   e.g. 10101111 = AF in hex
  //   Low Nibble
endmodule
