// Logisim project 2H_Bit_Reversal_Register.circ as structural Verilog: 1 circuit, main circuit main
module main (
  input  In0,
  input  In1,
  input  In2,
  input  In3,
  input  In4,
  input  In5,
  input  In6,
  input  In7,
  output Out7,
  output Out6,
  output Out5,
  output Out4,
  output Out3,
  output Out2,
  output Out1,
  output Out0
);


  assign Out0 = In0;
  assign Out1 = In1;
  assign Out2 = In2;
  assign Out3 = In3;
  assign Out4 = In4;
  assign Out5 = In5;
  assign Out6 = In6;
  assign Out7 = In7;

  // Notes on the sheet:
  //   Exercise 2H: 8-bit Bit Reversal
  //   In[i] maps to Out[7-i]
endmodule
