// Logisim project 5H_4bit_Comparator.circ as structural Verilog: 1 circuit, main circuit main
module main (
  input  [3:0] A_4bit,
  input  [3:0] B_4bit,
  output A_greater_B,
  output A_equals_B,
  output A_less_B
);

  Comparator #(.width(4)) comparator_1 (.a(A_4bit), .b(B_4bit), .gt(A_greater_B), .eq(A_equals_B), .lt(A_less_B));

  // Notes on the sheet:
  //   Exercise 5H: 4-bit Comparator
endmodule
