// Logisim project 7H_Priority_Encoder.circ as structural Verilog: 1 circuit, main circuit main
module main (
  input  I0,
  input  I1,
  input  I2,
  input  I3,
  output [1:0] Encoded,
  output Enable_Out,
  output Group_Signal
);

  Priority_Encoder #(.select(2)) priority_encoder_1 (
    .in1(I0), .in2(I1), .in3(I2), .out(Encoded), .gs(Enable_Out));  // open: in0, en_out, en_in

  // Notes on the sheet:
  //   Exercise 7H: 4-input Priority Encoder
  //   Outputs binary code of highest-priority active input
endmodule
