// Logisim project 8E_Single_LED_Control.circ as structural Verilog: 1 circuit, main circuit main
module main (
  input  Button
);

  LED led_1 (.in(Button));

  // Notes on the sheet:
  //   Exercise 8E: Single LED Control
  //   A button input directly drives an LED
endmodule
