// Logisim project 8H_8bit_Full_Adder.circ as structural Verilog: 1 circuit, main circuit main
module main (
  input  [7:0] A_8bit,
  input  [7:0] B_8bit,
  input  Carry_In,
  output [7:0] Sum,
  output Carry_Out
);

  Adder #(.width(8)) adder_1 (.a(A_8bit), .b(B_8bit), .cout(Carry_In));  // open: out, cin

  // Notes on the sheet:
  //   Exercise 8H: 8-bit Full Adder
endmodule
