// Logisim project AND_Gate.circ as structural Verilog: 1 circuit, main circuit main
module main (
  input  A,
  input  B,
  output Output
);

  and and_1 (Output, A, B);

  // Notes on the sheet:
  //   AND Gate
endmodule
