// Logisim project NOT_Gate.circ as structural Verilog: 1 circuit, main circuit main
module main (
  input  A,
  output Output
);

  not not_1 (Output, A);

  // Notes on the sheet:
  //   NOT Gate
endmodule
