// Logisim project OR_Gate.circ as structural Verilog: 1 circuit, main circuit main
module main (
  input  A,
  input  B,
  output Output
);

  or or_1 (Output, A, B);

  // Notes on the sheet:
  //   OR Gate
endmodule
