// Logisim project exercise5.circ as structural Verilog: 1 circuit, main circuit main
module main (
  input  A,
  input  B,
  input  C,
  input  D,
  output Output
);

  wire and_1_out, and_2_out, not_1_out;

  not not_1 (not_1_out, D);
  // AND_Gate and_1 has open pins: out=and_1_out
  buf and_2 (and_2_out, B);  // AND_Gate
  // OR_Gate or_1 has open pins: out=Output

  // Notes on the sheet:
  //   Exercise 5: F = AC + BCD'
endmodule
