// Logisim project exercise6.circ as structural Verilog: 1 circuit, main circuit main
module main (
  input  A,
  input  B,
  input  C,
  input  D,
  output Output
);

  wire and_1_out, and_2_out, not_1_out, not_2_out;

  not not_1 (not_1_out, B);
  not not_2 (not_2_out, D);
  // AND_Gate and_1 has open pins: out=and_1_out
  buf and_2 (and_2_out, not_1_out);  // AND_Gate
  // OR_Gate or_1 has open pins: out=Output

  // Notes on the sheet:
  //   Exercise 6: F = AC + AB'D'
endmodule
