// Logisim project karnaugh_2.circ as structural Verilog: 1 circuit, main circuit main
module main (
  input  A,
  input  B,
  input  C,
  input  D,
  output F
);

  wire and_1_out, and_2_out, not_1_out, not_2_out;

  not not_1 (not_1_out, B);
  not not_2 (not_2_out, C);
  and and_1 (and_1_out, C, D);
  and and_2 (and_2_out, A, not_2_out, D);
  or or_1 (F, and_1_out, and_2_out);
endmodule
