// Logisim project bcd_.circ as structural Verilog: 1 circuit, main circuit BCD_Adder
module BCD_Adder (
  input  A3,
  input  A2,
  input  A1,
  input  A0,
  input  B3,
  input  B2,
  input  B1,
  input  B0,
  input  Cin,
  output S0,
  output S1,
  output S2,
  output S3,
  output BCD_Cout
);

  wire adder_2_p1, adder_2_p3, adder_2_p4, CORRECT_out, undriven, undriven_2, undriven_3, undriven_4,
       undriven_5, Z8_Z2_out, Z8_Z4_out;

  // OR_Gate BCD_Cout has open pins: out=BCD_Cout
  or CORRECT (CORRECT_out, undriven, Z8_Z4_out, Z8_Z2_out);
  Adder #(.width(1)) adder_1 (.a(A3), .b(B3));  // open: out, cin, cout
  // Adder #(.width(1)) adder_2: pin names not known; wires that end beside it: adder_2_p1, 1'b0, adder_2_p3, adder_2_p4
  Adder #(.width(1)) adder_3 (.a(A2), .b(B2));  // open: out, cin, cout
  Adder #(.width(1)) adder_4 (.a(undriven_2), .b(undriven_3));  // open: out, cin, cout
  // AND_Gate Z8_Z4 has open pins: out=Z8_Z4_out
  // AND_Gate Z8_Z2 has open pins: out=Z8_Z2_out
  Adder #(.width(1)) adder_5 (.a(A1), .b(B1));  // open: out, cin, cout
  Adder #(.width(1)) adder_6 (.a(undriven_4), .b(CORRECT_out));  // open: out, cin, cout
  Adder #(.width(1)) adder_7 (.a(A0), .b(B0));  // open: out, cin, cout
  Adder #(.width(1)) adder_8 (.a(undriven_5), .b(1'b0));  // open: out, cin, cout

  // Notes on the sheet:
  //   BCD ADDER
endmodule
