// Logisim project bcd_add.circ as structural Verilog: 2 circuits, main circuit main
module BCD_Adder (
  input  [3:0] A,
  input  [3:0] B,
  input  Cin,
  output BCD_Cout,
  output [3:0] BCD_Sum
);

  wire S3_S1_out, S3_S2_out, undriven;
  wire [3:0] undriven_2, undriven_3;

  Adder #(.width(4)) adder_1 (.a(A), .b(B));  // open: out, cin, cout
  // AND_Gate S3_S2 has open pins: out=S3_S2_out
  // AND_Gate S3_S1 has open pins: out=S3_S1_out
  or CORRECT (BCD_Cout, undriven, S3_S2_out, S3_S1_out);
  Adder #(.width(4)) adder_2 (
    .a(undriven_2), .b({undriven_3[3], undriven_2[0], undriven_3[1:0]}));  // open: out, cin, cout
  // Pins of 1 and 4 bits meet at undriven_2
endmodule

module main (
  output BCD_Cout__exp_1,
  output [3:0] BCD_Sum__exp_5
);

  BCD_Adder bcd_adder_1 ();  // open: A, B, Cin, BCD_Cout, BCD_Sum
endmodule
